// Logisim project Single Cycle Processor.circ as structural Verilog: 10 circuits, main circuit ALU
module ALU (
  input  [15:0] A,
  input  [15:0] B,
  input  [15:0] I,
  input  Ci,
  input  [5:0] opcode,
  output Co,
  output [15:0] E
);

  wire and_2_out, clock_1_out, comparator_1_lt, n16_bit_adder_1_co, n16_bit_adder_2_co, nand_1_out,
       not_1_out, subtractor_1_bout, xnor_1_out, xnor_2_out, xnor_3_out, xnor_4_out;
  wire [15:0] and_1_out, bit_extender_3_out, divider_1_out, Hi_q, Lo_q, multiplier_1_out, multiplier_1_out_2,
       n16_bit_adder_1_s, n16_bit_adder_2_s, or_1_out, shifter_1_out, subtractor_1_out;
  wire [31:0] bit_extender_1_out, bit_extender_2_out;

  assign bit_extender_1_out = {{16{A[15]}}, A};  // Bit_Extender bit_extender_1
  assign bit_extender_2_out = {{16{B[15]}}, B};  // Bit_Extender bit_extender_2
  Divider #(.width(16)) divider_1 (.a(A), .b(B), .out(divider_1_out), .upper(A));  // open: rem
  Clock clock_1 (.out(clock_1_out));
  _16_Bit_Adder u_16_bit_adder_1 (.A(A), .B(B), .Ci(Ci), .Co(n16_bit_adder_1_co), .S(n16_bit_adder_1_s));
  assign or_1_out = B | A;  // OR_Gate or_1, 16 bits wide
  _16_Bit_Adder u_16_bit_adder_2 (.A(A), .B(I), .Ci(Ci), .Co(n16_bit_adder_2_co), .S(n16_bit_adder_2_s));
  Shifter #(.width(16)) shifter_1 (.in(A), .\dist (B[3:0]), .out(shifter_1_out));
  Comparator #(.width(16)) comparator_1 (.a(A), .b(B), .lt(comparator_1_lt));  // open: gt, eq
  Register #(.width(16), .trigger("high")) Hi (
    .D(multiplier_1_out_2), .en(and_2_out), .Q(Hi_q), .clk(clock_1_out));  // open: clr
  Register #(.width(16), .trigger("high")) Lo (
    .D(multiplier_1_out), .en(and_2_out), .Q(Lo_q), .clk(clock_1_out));  // open: clr
  Subtractor #(.width(16)) subtractor_1 (.a(A), .b(B), .out(subtractor_1_out), .bin(Ci), .bout(subtractor_1_bout));
  Multiplier #(.width(32)) multiplier_1 (
    .a(bit_extender_1_out), .b(bit_extender_2_out), .out({multiplier_1_out_2, multiplier_1_out}));  // open: cin, cout
  assign and_1_out = B & A;  // AND_Gate and_1, 16 bits wide
  not not_1 (not_1_out, 1'b1);
  assign bit_extender_3_out = {{15{1'b0}}, comparator_1_lt};  // Bit_Extender bit_extender_3
  Multiplexer #(.select(4), .width(16)) multiplexer_1 (
    .in0(n16_bit_adder_1_s), .in1(subtractor_1_out), .in3(and_1_out), .in4(or_1_out),
    .in5(n16_bit_adder_2_s), .in6(shifter_1_out), .in7(bit_extender_3_out), .in8(Hi_q), .in9(Lo_q),
    .in15(divider_1_out), .out(E), .sel(opcode[3:0]), .en(nand_1_out));  // open: in2, in10, in11, in12, in13, in14
  nand nand_1 (nand_1_out, opcode[4], opcode[5]);
  xnor xnor_1 (xnor_1_out, opcode[0], not_1_out);
  xnor xnor_2 (xnor_2_out, opcode[1], 1'b1);
  xnor xnor_3 (xnor_3_out, opcode[2], not_1_out);
  xnor xnor_4 (xnor_4_out, opcode[3], not_1_out);
  Multiplexer #(.select(4)) multiplexer_2 (
    .in0(n16_bit_adder_1_co), .in1(subtractor_1_bout), .in5(n16_bit_adder_2_co), .out(Co), .sel(opcode[3:0]),
    .en(nand_1_out));  // open: in2, in3, in4, in6, in7, in8, in9, in10, in11, in12, in13, in14, in15
  and and_2 (and_2_out, xnor_1_out, xnor_2_out, xnor_3_out, xnor_4_out);
endmodule

module _1_Bit_Full_Adder (
  input  A,
  input  B,
  input  Ci,
  output S,
  output Co
);

  wire and_1_out, and_2_out, xor_1_out;

  xor xor_1 (xor_1_out, A, B);
  xor xor_2 (S, xor_1_out, Ci);
  and and_1 (and_1_out, xor_1_out, Ci);
  and and_2 (and_2_out, A, B);
  or or_1 (Co, and_1_out, and_2_out);

  // Notes on the sheet:
  //   A: pull=up
endmodule

module _4_Bit_Full_Adder (
  input  [3:0] A,
  input  [3:0] B,
  input  Ci,
  output Co,
  output [3:0] S
);

  wire n1_bit_full_adder_1_co, n1_bit_full_adder_2_co, n1_bit_full_adder_3_co;

  _1_Bit_Full_Adder u_1_bit_full_adder_1 (.A(A[0]), .B(B[0]), .Ci(Ci), .S(S[0]), .Co(n1_bit_full_adder_1_co));
  _1_Bit_Full_Adder u_1_bit_full_adder_2 (
    .A(A[1]), .B(B[1]), .Ci(n1_bit_full_adder_1_co), .S(S[1]), .Co(n1_bit_full_adder_2_co));
  _1_Bit_Full_Adder u_1_bit_full_adder_3 (
    .A(A[2]), .B(B[2]), .Ci(n1_bit_full_adder_2_co), .S(S[2]), .Co(n1_bit_full_adder_3_co));
  _1_Bit_Full_Adder u_1_bit_full_adder_4 (.A(A[3]), .B(B[3]), .Ci(n1_bit_full_adder_3_co), .S(S[3]), .Co(Co));
endmodule

module _16_Bit_Immidiate_adder (
  input  [15:0] A,
  input  Ci,
  input  [7:0] Ext,
  output [15:0] S,
  output Co
);

  wire n16_bit_adder_1_co;
  wire [15:0] bit_extender_1_out;

  assign bit_extender_1_out = {{8{Ext[7]}}, Ext};  // Bit_Extender bit_extender_1
  _16_Bit_Adder u_16_bit_adder_1 (.A(A), .B(bit_extender_1_out), .Ci(Ci), .Co(n16_bit_adder_1_co), .S(S));
endmodule

module _16_Bit_Adder (
  input  [15:0] A,
  input  [15:0] B,
  input  Ci,
  output Co,
  output [15:0] S
);

  wire n4_bit_full_adder_1_co, n4_bit_full_adder_2_co, n4_bit_full_adder_3_co;

  _4_Bit_Full_Adder u_4_bit_full_adder_1 (.A(A[3:0]), .B(B[3:0]), .Ci(Ci), .Co(n4_bit_full_adder_1_co), .S(S[3:0]));
  _4_Bit_Full_Adder u_4_bit_full_adder_2 (
    .A(A[7:4]), .B(B[7:4]), .Ci(n4_bit_full_adder_1_co), .Co(n4_bit_full_adder_2_co), .S(S[7:4]));
  _4_Bit_Full_Adder u_4_bit_full_adder_3 (
    .A(A[11:8]), .B(B[11:8]), .Ci(n4_bit_full_adder_2_co), .Co(n4_bit_full_adder_3_co), .S(S[11:8]));
  _4_Bit_Full_Adder u_4_bit_full_adder_4 (
    .A(A[15:12]), .B(B[15:12]), .Ci(n4_bit_full_adder_3_co), .Co(Co), .S(S[15:12]));
endmodule

// Reg
module Register_File (
  input  [3:0] ReadRegister_1,
  input  [3:0] Write_Register,
  input  [3:0] ReadRegister_2,
  input  [15:0] Write_Data,
  input  regWrite,
  output [15:0] ReadData_1,
  output [15:0] ReadData_2
);

  wire and_1_out, and_2_out, and_3_out, and_4_out, and_5_out, and_6_out, and_7_out, and_8_out, and_9_out,
       and_10_out, and_11_out, and_12_out, and_13_out, and_14_out, and_15_out, and_16_out, clock_1_out,
       decoder_1_out0, decoder_1_out1, decoder_1_out2, decoder_1_out3, decoder_1_out4, decoder_1_out5,
       decoder_1_out6, decoder_1_out7, decoder_1_out8, decoder_1_out9, decoder_1_out10, decoder_1_out11,
       decoder_1_out12, decoder_1_out13, decoder_1_out14, decoder_1_out15, undriven, undriven_2;
  wire [15:0] register_1_q, register_2_q, register_3_q, register_4_q, register_5_q, register_6_q,
       register_7_q, register_8_q, register_9_q, register_10_q, register_11_q, register_12_q, register_13_q,
       register_14_q, register_15_q, register_16_q;

  Decoder #(.select(4)) decoder_1 (
    .out0(decoder_1_out0), .out1(decoder_1_out1), .out2(decoder_1_out2), .out3(decoder_1_out3),
    .out4(decoder_1_out4), .out5(decoder_1_out5), .out6(decoder_1_out6), .out7(decoder_1_out7),
    .out8(decoder_1_out8), .out9(decoder_1_out9), .out10(decoder_1_out10), .out11(decoder_1_out11),
    .out12(decoder_1_out12), .out13(decoder_1_out13), .out14(decoder_1_out14), .out15(decoder_1_out15),
    .sel(Write_Register));  // open: en
  and and_1 (and_1_out, decoder_1_out0, regWrite);
  and and_2 (and_2_out, decoder_1_out1, regWrite);
  and and_3 (and_3_out, decoder_1_out2, regWrite);
  and and_4 (and_4_out, decoder_1_out3, regWrite);
  and and_5 (and_5_out, decoder_1_out4, regWrite);
  and and_6 (and_6_out, decoder_1_out5, regWrite);
  and and_7 (and_7_out, decoder_1_out6, regWrite);
  and and_8 (and_8_out, decoder_1_out7, regWrite);
  Clock clock_1 (.out(clock_1_out));
  Register #(.width(16)) register_1 (
    .D(Write_Data), .en(and_1_out), .Q(register_1_q), .clk(clock_1_out), .clr(undriven));
  Register #(.width(16)) register_2 (
    .D(Write_Data), .en(and_2_out), .Q(register_2_q), .clk(clock_1_out), .clr(undriven_2));
  Register #(.width(16)) register_3 (.D(Write_Data), .en(and_3_out), .Q(register_3_q), .clk(clock_1_out));  // open: clr
  Register #(.width(16)) register_4 (.D(Write_Data), .en(and_4_out), .Q(register_4_q), .clk(clock_1_out));  // open: clr
  Register #(.width(16)) register_5 (.D(Write_Data), .en(and_5_out), .Q(register_5_q), .clk(clock_1_out));  // open: clr
  Register #(.width(16)) register_6 (.D(Write_Data), .en(and_6_out), .Q(register_6_q), .clk(clock_1_out));  // open: clr
  Register #(.width(16)) register_7 (.D(Write_Data), .en(and_7_out), .Q(register_7_q), .clk(clock_1_out));  // open: clr
  Register #(.width(16)) register_8 (.D(Write_Data), .en(and_8_out), .Q(register_8_q), .clk(clock_1_out));  // open: clr
  and and_9 (and_9_out, decoder_1_out8, regWrite);
  and and_10 (and_10_out, decoder_1_out9, regWrite);
  and and_11 (and_11_out, decoder_1_out10, regWrite);
  and and_12 (and_12_out, decoder_1_out11, regWrite);
  and and_13 (and_13_out, decoder_1_out12, regWrite);
  and and_14 (and_14_out, decoder_1_out13, regWrite);
  and and_15 (and_15_out, decoder_1_out14, regWrite);
  and and_16 (and_16_out, decoder_1_out15, regWrite);
  Register #(.width(16)) register_9 (.D(Write_Data), .en(and_9_out), .Q(register_9_q), .clk(clock_1_out));  // open: clr
  Register #(.width(16)) register_10 (
    .D(Write_Data), .en(and_10_out), .Q(register_10_q), .clk(clock_1_out));  // open: clr
  Register #(.width(16)) register_11 (
    .D(Write_Data), .en(and_11_out), .Q(register_11_q), .clk(clock_1_out));  // open: clr
  Register #(.width(16)) register_12 (
    .D(Write_Data), .en(and_12_out), .Q(register_12_q), .clk(clock_1_out));  // open: clr
  Register #(.width(16)) register_13 (
    .D(Write_Data), .en(and_13_out), .Q(register_13_q), .clk(clock_1_out));  // open: clr
  Register #(.width(16)) register_14 (
    .D(Write_Data), .en(and_14_out), .Q(register_14_q), .clk(clock_1_out));  // open: clr
  Register #(.width(16)) register_15 (
    .D(Write_Data), .en(and_15_out), .Q(register_15_q), .clk(clock_1_out));  // open: clr
  Register #(.width(16)) register_16 (
    .D(Write_Data), .en(and_16_out), .Q(register_16_q), .clk(clock_1_out));  // open: clr
  Multiplexer #(.select(4), .width(16)) multiplexer_1 (
    .in0(register_1_q), .in1(register_2_q), .in2(register_3_q), .in3(register_4_q), .in4(register_5_q),
    .in5(register_6_q), .in6(register_7_q), .in7(register_8_q), .in8(register_9_q), .in9(register_10_q),
    .in10(register_11_q), .in11(register_12_q), .in12(register_13_q), .in13(register_14_q),
    .in14(register_15_q), .in15(register_16_q), .out(ReadData_1), .sel(ReadRegister_1));  // open: en
  Multiplexer #(.select(4), .width(16)) multiplexer_2 (
    .in0(register_1_q), .in1(register_2_q), .in2(register_3_q), .in3(register_4_q), .in4(register_5_q),
    .in5(register_6_q), .in6(register_7_q), .in7(register_8_q), .in8(register_9_q), .in9(register_10_q),
    .in10(register_11_q), .in11(register_12_q), .in12(register_13_q), .in13(register_14_q),
    .in14(register_15_q), .in15(register_16_q), .out(ReadData_2), .sel(ReadRegister_2));  // open: en
endmodule

module CPU (
  input  [15:0] nextPC,
  input  in_2,
  input  in_3
);

  wire clock_1_out, control_unit_1_alusrc, control_unit_1_jump, control_unit_1_memread,
       control_unit_1_memtoreg, control_unit_1_memwrite, control_unit_1_pcsrc, control_unit_1_regdst,
       control_unit_1_regwrite;
  wire [3:0] multiplexer_1_out;
  wire [15:0] adder_1_out, ALU_e, Data_Memory_read_data, multiplexer_2_out, multiplexer_3_out,
       multiplexer_4_out, multiplexer_5_out, n16_bit_adder_1_s, PC_q, register_file_1_readdata_1,
       register_file_1_readdata_2, shifter_1_out;
  wire [31:0] rom_1_data;

  Register #(.width(16)) PC (.D(multiplexer_3_out), .en(in_3), .Q(PC_q), .clk(clock_1_out));  // open: clr
  Clock clock_1 (.out(clock_1_out));
  _16_Bit_Adder u_16_bit_adder_1 (.A(nextPC), .B(PC_q), .Ci(in_2), .S(n16_bit_adder_1_s));  // open: Co
  ROM #(.addrWidth(16), .dataWidth(32)) rom_1 (.addr(PC_q), .data(rom_1_data));  // open: sel
  Control_Unit control_unit_1 (
    .opcode(rom_1_data[5:0]), .RegDst(control_unit_1_regdst), .AluSrc(control_unit_1_alusrc),
    .RegWrite(control_unit_1_regwrite), .MemWrite(control_unit_1_memwrite), .PCSrc(control_unit_1_pcsrc),
    .MemToReg(control_unit_1_memtoreg), .MemRead(control_unit_1_memread), .Jump(control_unit_1_jump));
  Adder #(.width(16)) adder_1 (.a(shifter_1_out), .b(n16_bit_adder_1_s), .out(adder_1_out), .cin(in_2));  // open: cout
  Multiplexer #(.width(4)) multiplexer_1 (
    .in0(rom_1_data[19:16]), .in1(rom_1_data[14:11]), .out(multiplexer_1_out), .sel(control_unit_1_regdst));  // open: en
  Multiplexer #(.width(16)) multiplexer_2 (
    .in0(n16_bit_adder_1_s), .in1(adder_1_out), .out(multiplexer_2_out), .sel(control_unit_1_pcsrc));  // open: en
  Register_File register_file_1 (
    .Write_Register(multiplexer_1_out), .Write_Data(multiplexer_5_out), .regWrite(control_unit_1_regwrite),
    .ReadRegister_1(rom_1_data[24:21]), .ReadRegister_2(rom_1_data[19:16]),
    .ReadData_1(register_file_1_readdata_1), .ReadData_2(register_file_1_readdata_2));
  Multiplexer #(.width(16)) multiplexer_3 (
    .in0(multiplexer_2_out), .in1(rom_1_data[15:0]), .out(multiplexer_3_out), .sel(control_unit_1_jump));  // open: en
  Multiplexer #(.width(16)) multiplexer_4 (
    .in0(register_file_1_readdata_2), .in1(rom_1_data[15:0]), .out(multiplexer_4_out),
    .sel(control_unit_1_alusrc));  // open: en
  Shifter #(.width(16)) shifter_1 (.in(rom_1_data[15:0]), .\dist (4'b0010), .out(shifter_1_out));
  ALU ALU (
    .A(register_file_1_readdata_1), .B(multiplexer_4_out), .I(rom_1_data[15:0]), .Ci(in_2),
    .opcode(rom_1_data[31:26]), .E(ALU_e));  // open: Co
  Data_Memory Data_Memory (
    .Address(ALU_e), .Write_Data(register_file_1_readdata_2), .clock(clock_1_out),
    .MemRead(control_unit_1_memread), .MemWrite(control_unit_1_memwrite), .Read_Data(Data_Memory_read_data));
  Multiplexer #(.width(16)) multiplexer_5 (
    .in0(ALU_e), .in1(Data_Memory_read_data), .out(multiplexer_5_out), .sel(control_unit_1_memtoreg));  // open: en

  // Notes on the sheet:
  //   contents of rom_1 (hex, n*v repeats v):
  //   0 100010 11000 13*0 100 100010 100000 111111 11*0 11111111 1000 15*0 1100 15*0 10000 100010 11000
  //   13*0 10100 15*0 11000 15*0 11100 15*0 100000 15*0 100100 15*0 101000 15*0 101100 15*0 110000 15*0
  //   110100 15*0 111000 15*0 111100
  //   RegDst
  //   PCSrc
  //   RegWrite
  //   Jump
  //   MemRead
  //   AluSrc
  //   MemWrite
  //   MemToReg
endmodule

// DM
module Data_Memory (
  input  [15:0] Address,
  input  [15:0] Write_Data,
  input  clock,
  input  MemRead,
  input  MemWrite,
  output [15:0] Read_Data
);

  RAM #(.addrWidth(16), .dataWidth(16), .bus("separate")) ram_1 (
    .addr(Address), .din(Write_Data), .data(Read_Data), .str(MemWrite), .clk(clock), .ld(MemRead));  // open: sel, clr
endmodule

// IM
module Instruction_Memory (
  input  [15:0] Read_Address,
  output [31:0] Instruction
);

  ROM #(.addrWidth(16), .dataWidth(32)) rom_1 (.addr(Read_Address), .data(Instruction));  // open: sel

  // Notes on the sheet:
  //   contents of rom_1 (hex, n*v repeats v):
  //   0 100010 11000 13*0 100 100010 100000 13*0 1000 15*0 1100 15*0 10000 15*0 10100 15*0 11000 15*0
  //   11100 15*0 100000 15*0 100100 15*0 101000 15*0 101100 15*0 110000 15*0 110100 15*0 111000 15*0
  //   111100
endmodule

// CU
module Control_Unit (
  input  [5:0] opcode,
  output RegDst,
  output AluSrc,
  output MemToReg,
  output RegWrite,
  output MemRead,
  output MemWrite,
  output PCSrc,
  output Jump
);

  wire and_1_out, and_2_out, and_3_out, and_4_out, and_5_out, and_6_out, and_7_out, and_8_out, and_10_out,
       and_11_out, and_12_out, and_13_out, and_14_out, and_15_out, not_1_out, not_2_out, not_3_out,
       not_4_out, not_5_out, not_6_out, not_7_out, not_8_out, not_9_out, not_10_out, not_11_out, not_12_out,
       not_13_out, not_14_out, not_15_out, not_16_out, not_17_out, not_18_out, not_19_out, not_20_out,
       not_21_out, not_22_out, not_23_out, not_24_out, not_25_out, not_26_out, not_27_out;

  and and_1 (and_1_out, not_1_out, not_3_out, not_2_out);
  not not_1 (not_1_out, opcode[1]);
  not not_2 (not_2_out, opcode[3]);
  not not_3 (not_3_out, opcode[2]);
  and and_2 (and_2_out, opcode[0], opcode[1], opcode[2], opcode[3]);
  and and_3 (and_3_out, opcode[1], opcode[2], not_9_out);
  or or_1 (RegDst, and_1_out, and_2_out, and_3_out, and_5_out, and_4_out, and_6_out);
  and and_4 (and_4_out, not_6_out, not_4_out, opcode[3]);
  and and_5 (and_5_out, not_8_out, not_5_out, not_7_out);
  not not_4 (not_4_out, opcode[2]);
  not not_5 (not_5_out, opcode[1]);
  not not_6 (not_6_out, opcode[1]);
  not not_7 (not_7_out, opcode[3]);
  not not_8 (not_8_out, opcode[0]);
  not not_9 (not_9_out, opcode[3]);
  and and_6 (and_6_out, opcode[0], opcode[1], not_10_out);
  not not_10 (not_10_out, opcode[3]);
  or or_2 (AluSrc, and_7_out, and_8_out);
  and and_7 (and_7_out, opcode[0], not_11_out, opcode[2]);
  and and_8 (and_8_out, opcode[1], not_12_out, opcode[3]);
  not not_11 (not_11_out, opcode[1]);
  not not_12 (not_12_out, opcode[2]);
  and and_9 (MemToReg, not_14_out, opcode[1], not_13_out, opcode[3]);
  not not_13 (not_13_out, opcode[2]);
  not not_14 (not_14_out, opcode[0]);
  and and_10 (and_10_out, opcode[0], opcode[1], opcode[2], opcode[3]);
  and and_11 (and_11_out, opcode[0], opcode[1], not_19_out);
  and and_12 (and_12_out, not_15_out, not_16_out);
  not not_15 (not_15_out, opcode[1]);
  not not_16 (not_16_out, opcode[3]);
  or or_3 (RegWrite, and_10_out, and_12_out, and_11_out, and_13_out, and_14_out, and_15_out);
  and and_13 (and_13_out, opcode[1], opcode[2], not_18_out);
  and and_14 (and_14_out, not_20_out, not_17_out, opcode[3]);
  not not_17 (not_17_out, opcode[2]);
  not not_18 (not_18_out, opcode[3]);
  not not_19 (not_19_out, opcode[3]);
  not not_20 (not_20_out, opcode[1]);
  and and_15 (and_15_out, not_21_out, opcode[1], not_22_out, opcode[3]);
  not not_21 (not_21_out, opcode[0]);
  not not_22 (not_22_out, opcode[2]);
  and and_16 (MemRead, not_23_out, opcode[1], not_24_out, opcode[3]);
  not not_23 (not_23_out, opcode[0]);
  not not_24 (not_24_out, opcode[2]);
  and and_17 (MemWrite, opcode[0], opcode[1], not_26_out, opcode[3]);
  and and_18 (PCSrc, not_25_out, opcode[2], opcode[3]);
  not not_25 (not_25_out, opcode[1]);
  not not_26 (not_26_out, opcode[2]);
  and and_19 (Jump, not_27_out, opcode[1], opcode[2], opcode[3]);
  not not_27 (not_27_out, opcode[0]);
endmodule
